# Fritzing sketch vib_belt_ci (saved by Fritzing 0.9.2b)

parts:
  Part1 = Arduino Mega 2560 (Rev3)
  IC1 = ULN2003A [package="DIP16 [THT]"]
  IC2 = Voltage Regulator [package=78xxl]
  C2 = Electrolytic Capacitor [capacitance=4.7µF package="100 mil [THT, electrolytic]"]
  Power_plug1 = Power plug
  U3 = Vibration Motor- ROB-08449 [package=vibe-motor-10mm]
  U5 = Vibration Motor- ROB-08449 [package=vibe-motor-10mm]
  U7 = Vibration Motor- ROB-08449 [package=vibe-motor-10mm]
  U11 = Vibration Motor- ROB-08449 [package=vibe-motor-10mm]
  U9 = Vibration Motor- ROB-08449 [package=vibe-motor-10mm]
  U12 = Vibration Motor- ROB-08449 [package=vibe-motor-10mm]
  U2 = Vibration Motor- ROB-08449 [package=vibe-motor-10mm]
  U4 = Vibration Motor- ROB-08449 [package=vibe-motor-10mm]
  U6 = Vibration Motor- ROB-08449 [package=vibe-motor-10mm]
  U8 = Vibration Motor- ROB-08449 [package=vibe-motor-10mm]
  U10 = Vibration Motor- ROB-08449 [package=vibe-motor-10mm]
  C3 = Electrolytic Capacitor [capacitance=4.7µF package="100 mil [THT, electrolytic]"]
  U1 = Vibration Motor- ROB-08449 [package=vibe-motor-10mm]

nets:
  N1: Part1.D42, IC1.In_2
  N2: Part1.D44, IC1.In_3
  N3: Part1.D46, IC1.In_4
  N4: Part1.D48, IC1.In_5
  N5: Part1.D50, IC1.In_6
  N6: Part1.D52, IC1.In_7
  GND: Part1.GND, IC1.0V, IC2.GND, C2.-, Power_plug1.GND, C3.-
  N7: IC1.COM_-_Common, IC2.OUT, C2.+, U3.-, U5.-, U7.-, U11.-, U9.-, U12.-, U2.-, U4.-, U6.-, U8.-, U10.-, U1.-
  N8: IC1.Out_7, U11.+, U12.+
  N9: IC1.Out_6, U9.+, U10.+
  N10: IC1.Out_5, U7.+, U8.+
  N11: IC1.Out_4, U5.+, U6.+
  N12: IC1.Out_3, U3.+, U4.+
  N13: IC1.Out_2, U2.+, U1.+
  N14: IC2.IN, Power_plug1.VCC, C3.+

notes:
  Considering Vibration Motor's red cable as + and black as -
  9V input
